# Fritzing sketch FootPedalKeyboard Fritzing Sketch (saved by Fritzing 0.9.3b)
breadboards: 2

parts:
  Teensy_3_1 = Teensy 3.1  # not connected
  R1 = Resistor [tolerance=±5% resistance=100 package=THT]
  R2 = Resistor [tolerance=±5% resistance=100 package=THT]
  R3 = Resistor [tolerance=±5% resistance=100 package=THT]
  R4 = Resistor [tolerance=±5% resistance=100 package=THT]
  R5 = Resistor [tolerance=±5% resistance=100 package=THT]
  LED3 = smd LED [color="Red (660nm)" package="1206 [SMD]"]
  LED5 = smd LED [color="Blue (505nm)" package="1206 [SMD]"]
  LED6 = smd LED [color="Green (570nm)" package="1206 [SMD]"]
  LED7 = smd LED [color="White (4500K)" package="1206 [SMD]"]
  LED8 = smd LED [color="Orange (620nm)" package="1206 [SMD]"]

nets:
  N1: R1.Pin_1, LED5.anode
  N2: R2.Pin_1, LED6.anode
  N3: R3.Pin_1, LED7.anode
  N4: R4.Pin_1, LED8.anode
  N5: R5.Pin_1, LED3.anode
  N6: LED3.cathode, LED5.cathode, LED6.cathode, LED7.cathode, LED8.cathode

notes:
  LEDS
  A B C D E
  INPUT FROM KORG
  GND ABCDE
